# Fritzing sketch blender (saved by Fritzing 0.9.2b)
breadboards: 1

parts:
  IC2 = IC, DIP package, 40 pins [chip_label=WDC65C02S spacing=600mil]
  Raspberry_Pi2 = Raspberry Pi 2

nets:
  3V3: IC2.pin1, IC2.pin8, Raspberry_Pi2.3v3, Raspberry_Pi2.3V3
  N1: IC2.pin9, Raspberry_Pi2.GPIO4
  N2: IC2.pin10, Raspberry_Pi2.GPIO17
  N3: IC2.pin11, Raspberry_Pi2.GPIO27
  N4: IC2.pin12, Raspberry_Pi2.GPIO22
  N5: IC2.pin13, Raspberry_Pi2.GPIO10
  N6: IC2.pin14, Raspberry_Pi2.GPIO9
  N7: IC2.pin15, Raspberry_Pi2.GPIO11
  N8: IC2.pin16, Raspberry_Pi2.GPIO5
  N9: IC2.pin17, Raspberry_Pi2.GPIO6
  N10: IC2.pin18, Raspberry_Pi2.GPIO13
  N11: IC2.pin19, Raspberry_Pi2.GPIO19
  N12: IC2.pin20, Raspberry_Pi2.GPIO26
  N13: IC2.pin21, Raspberry_Pi2.GND
  N14: IC2.pin22, Raspberry_Pi2.GPIO21
  N15: IC2.pin23, Raspberry_Pi2.GPIO20
  N16: IC2.pin24, Raspberry_Pi2.GPIO16
  N17: IC2.pin25, Raspberry_Pi2.GPIO12
  N18: IC2.pin36, Raspberry_Pi2.GPIO7
  N19: IC2.pin40, Raspberry_Pi2.GPIO8

notes:
  VPB and VDD are connected to 3.3v, is that correct?
